# Fritzing sketch schema (saved by Fritzing 0.9.6b)
breadboards: 1

parts:
  D6 = Rectifier Diode [part_number=1N4001 package="300 mil [THT]"]
  D7 = Rectifier Diode [part_number=1N4001 package="300 mil [THT]"]
  D8 = Rectifier Diode [part_number=1N4001 package="300 mil [THT]"]
  D9 = Rectifier Diode [part_number=1N4001 package="300 mil [THT]"]
  WATER_PUMP5 = water pump/motor
  WATER_PUMP6 = water pump/motor
  WATER_PUMP7 = water pump/motor
  WATER_PUMP8 = water pump/motor
  U3 = Module 4 Relais 5V [package="Module 4 Relais 5V"]
  U4 = ESP8266 NodeMCU LoLin module
  Capacitive_Soil_Moisture_Sensor8 = DFRobot Capacitive Soil Moisture Sensor V1.0 [part_number=SEN0193]
  Capacitive_Soil_Moisture_Sensor9 = DFRobot Capacitive Soil Moisture Sensor V1.0 [part_number=SEN0193]
  Capacitive_Soil_Moisture_Sensor10 = DFRobot Capacitive Soil Moisture Sensor V1.0 [part_number=SEN0193]
  Capacitive_Soil_Moisture_Sensor11 = DFRobot Capacitive Soil Moisture Sensor V1.0 [part_number=SEN0193]

nets:
  N1: D6.cathode, D7.cathode, D8.cathode, D9.cathode, U4.A0
  N2: D9.anode, Capacitive_Soil_Moisture_Sensor10.A
  GND: WATER_PUMP5.pin_1, WATER_PUMP6.pin_1, WATER_PUMP7.pin_1, WATER_PUMP8.pin_1, U3.GND, U4.GND, Capacitive_Soil_Moisture_Sensor8.GND, Capacitive_Soil_Moisture_Sensor9.GND, Capacitive_Soil_Moisture_Sensor10.GND, Capacitive_Soil_Moisture_Sensor11.GND
  N3: WATER_PUMP5.pin_2, U3.K1-NF
  N4: WATER_PUMP6.pin_2, U3.K2-NF
  N5: WATER_PUMP7.pin_2, WATER_PUMP8.pin_2, U3.K3-NF
  N6: U3.VCC, U3.K1-NO, U3.K2-NO, U3.K3-NO, U4.VU
  N7: U3.IN1, U4.D0
  N8: U3.IN2, U4.D1
  N9: U3.IN3, U4.D2
  N10: U4.D5, Capacitive_Soil_Moisture_Sensor11.VCC
  N11: U4.D6, Capacitive_Soil_Moisture_Sensor10.VCC
  N12: U4.D7, Capacitive_Soil_Moisture_Sensor8.VCC
  N13: U4.D8, Capacitive_Soil_Moisture_Sensor9.VCC

custom parts:
  water pump/motor: WATER PUMP BY ARDUBLOCKTR
  Module 4 Relais 5V: Module 4 Relais 5V 4x SPD-06VDC-SD-C
  ESP8266 NodeMCU LoLin module: ESP8266 based NodeMCU
  DFRobot Capacitive Soil Moisture Sensor V1.0: DFRobot Capacitive Soil Moisture Sensor V1.0 This product measures soil moisture levels by capacitive sensing, rather than resistive sensing like other types of moisture sensor. It is made of a corrosion resistant material giving it a long service life. Insert it into soil and impress your friends with the real-time soil moisture data! The product includes an on-board voltage regulator which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
